// Logisim project ArquiteturaDeComputadores.circ as structural Verilog: 16 circuits, main circuit main
module main (
);

  wire button_1_out, clock_1_out, d_ff_1_q, d_ff_2_q, not_1_out, not_2_out, ula_1_overflow, ula_1_zero,
       unidade_de_controle_1_clk_ac, unidade_de_controle_1_clk_pc, unidade_de_controle_1_clk_ram,
       unidade_de_controle_1_clk_ri, \unidade_de_controle_1_direção , unidade_de_controle_1_e,
       unidade_de_controle_1_load, unidade_de_controle_1_out_17, unidade_de_controle_1_rst_pc;
  wire [2:0] \unidade_de_controle_1_operação ;
  wire [3:0] counter_1_q, mux_1_out_4, ram_1_data, reg_ac_1_d_2, ula_1_out_6,
       \unidade_de_controle_1_b_endereços , unidade_de_controle_1_dado, unidade_de_controle_1_operando;
  wire [7:0] ir_1_d_2, rom_1_data;

  not not_1 (not_1_out, unidade_de_controle_1_load);
  Unidade_de_controle unidade_de_controle_1 (
    .\B_Endereços (\unidade_de_controle_1_b_endereços ), .Operando(unidade_de_controle_1_operando),
    .\Direção (\unidade_de_controle_1_direção ), .E(unidade_de_controle_1_e),
    .\Operação (\unidade_de_controle_1_operação ), .\Instrução (ir_1_d_2), .Clock(clock_1_out),
    .Reset(button_1_out), .Rst_PC(unidade_de_controle_1_rst_pc), .clk_RI(unidade_de_controle_1_clk_ri),
    .clk_PC(unidade_de_controle_1_clk_pc), .clk_AC(unidade_de_controle_1_clk_ac),
    .clk_RAM(unidade_de_controle_1_clk_ram), .Zero(d_ff_2_q), .Load(unidade_de_controle_1_load),
    .Overflow(d_ff_1_q), .Dado(unidade_de_controle_1_dado), .out_17(unidade_de_controle_1_out_17));
  Clock clock_1 (.out(clock_1_out));
  // Probe on ir_1_d_2
  IR ir_1 (.D_2(ir_1_d_2), .D(rom_1_data), .Clock(unidade_de_controle_1_clk_ri));
  ROM #(.addrWidth(4)) rom_1 (.addr(counter_1_q), .data(rom_1_data));  // open: sel
  Counter #(.width(4), .max('hf), .trigger("falling")) counter_1 (
    .load(unidade_de_controle_1_load), .D(unidade_de_controle_1_dado), .count(not_1_out), .Q(counter_1_q),
    .clk(unidade_de_controle_1_clk_pc), .clr(unidade_de_controle_1_rst_pc));  // open: carry
  Button button_1 (.out(button_1_out));
  // Probe on reg_ac_1_d_2
  MUX mux_1 (
    .E(unidade_de_controle_1_operando), .in_3(\unidade_de_controle_1_direção ), .D(ram_1_data),
    .out_4(mux_1_out_4));
  ULA ula_1 (
    .D(unidade_de_controle_1_e), .A(reg_ac_1_d_2), .B(mux_1_out_4),
    .\Operações (\unidade_de_controle_1_operação ), .out_6(ula_1_out_6), .Overflow(ula_1_overflow),
    .Zero(ula_1_zero));
  // Probe on ula_1_out_6
  REG_AC reg_ac_1 (.D(ula_1_out_6), .D_2(reg_ac_1_d_2), .Clock(unidade_de_controle_1_clk_ac));
  D_Flip_Flop d_ff_1 (
    .clk(unidade_de_controle_1_clk_ac), .D(ula_1_overflow), .Q(d_ff_1_q));  // open: Qn, preset, en, reset
  D_Flip_Flop d_ff_2 (.clk(unidade_de_controle_1_clk_ac), .D(ula_1_zero), .Q(d_ff_2_q));  // open: Qn, preset, en, reset
  RAM #(.addrWidth(4), .dataWidth(4)) ram_1 (
    .addr(\unidade_de_controle_1_b_endereços ), .data(ram_1_data), .clk(unidade_de_controle_1_clk_ram),
    .ld(unidade_de_controle_1_out_17));  // open: sel, clr
  not not_2 (not_2_out, unidade_de_controle_1_out_17);
  Buffer buffer_1 (.in_1(reg_ac_1_d_2), .out_3(ram_1_data), .in_2(not_2_out));

  // Notes on the sheet:
  //   contents of rom_1 (hex, n*v repeats v):
  //   0 f0 1 f1 10 31 d0 f2 11 f0 12 f1 e4
endmodule

module Add1 (
  input  A,
  input  B,
  input  CARRY_IN,
  output S,
  output CARRY_OUT
);

  wire and_1_out, and_2_out, or_1_out, xor_1_out;

  xor xor_1 (xor_1_out, A, B);
  or or_1 (or_1_out, B, CARRY_IN);
  xor xor_2 (S, xor_1_out, CARRY_IN);
  and and_1 (and_1_out, B, CARRY_IN);
  and and_2 (and_2_out, or_1_out, A);
  or or_2 (CARRY_OUT, and_2_out, and_1_out);
endmodule

module Add4 (
  input  [3:0] A,
  input  [3:0] B,
  input  CARRY_IN,
  output OVERFLOW,
  output [3:0] SOMA
);

  wire add1_2_carry_out, add1_3_carry_out, add1_4_carry_out;

  Add1 add1_1 (.A(A[3]), .B(B[3]), .CARRY_IN(add1_2_carry_out), .S(SOMA[3]), .CARRY_OUT(OVERFLOW));
  Add1 add1_2 (.A(A[2]), .B(B[2]), .CARRY_IN(add1_3_carry_out), .S(SOMA[2]), .CARRY_OUT(add1_2_carry_out));
  Add1 add1_3 (.A(A[1]), .B(B[1]), .CARRY_IN(add1_4_carry_out), .S(SOMA[1]), .CARRY_OUT(add1_3_carry_out));
  Add1 add1_4 (.A(A[0]), .B(B[0]), .CARRY_IN(CARRY_IN), .S(SOMA[0]), .CARRY_OUT(add1_4_carry_out));
endmodule

module Sub1 (
  input  A,
  input  B,
  input  CARRY_IN,
  output S,
  output CARRY_OUT
);

  wire and_1_out, and_2_out, not_1_out, or_1_out, xor_1_out;

  xor xor_1 (xor_1_out, A, B);
  or or_1 (or_1_out, B, CARRY_IN);
  xor xor_2 (S, xor_1_out, CARRY_IN);
  not not_1 (not_1_out, A);
  and and_1 (and_1_out, B, CARRY_IN);
  and and_2 (and_2_out, or_1_out, not_1_out);
  or or_2 (CARRY_OUT, and_2_out, and_1_out);
endmodule

module Sub4 (
  input  [3:0] A,
  input  [3:0] B,
  input  CARRY_IN,
  output OVERFLOW,
  output [3:0] \SUBTRAÇÃO 
);

  wire sub1_2_carry_out, sub1_3_carry_out, sub1_4_carry_out;

  Sub1 sub1_1 (.A(A[3]), .B(B[3]), .CARRY_IN(sub1_2_carry_out), .S(\SUBTRAÇÃO [3]), .CARRY_OUT(OVERFLOW));
  Sub1 sub1_2 (.A(A[2]), .B(B[2]), .CARRY_IN(sub1_3_carry_out), .S(\SUBTRAÇÃO [2]), .CARRY_OUT(sub1_2_carry_out));
  Sub1 sub1_3 (.A(A[1]), .B(B[1]), .CARRY_IN(sub1_4_carry_out), .S(\SUBTRAÇÃO [1]), .CARRY_OUT(sub1_3_carry_out));
  Sub1 sub1_4 (.A(A[0]), .B(B[0]), .CARRY_IN(CARRY_IN), .S(\SUBTRAÇÃO [0]), .CARRY_OUT(sub1_4_carry_out));
endmodule

module Buffer (
  input  [3:0] in_1,
  input  in_2,
  output [3:0] out_3
);

  assign out_3[3] = in_2 ? in_1[3] : 1'bz;  // Controlled_Buffer controlled_buffer_1
  assign out_3[2] = in_2 ? in_1[2] : 1'bz;  // Controlled_Buffer controlled_buffer_2
  assign out_3[0] = in_2 ? in_1[0] : 1'bz;  // Controlled_Buffer controlled_buffer_3
  assign out_3[1] = in_2 ? in_1[1] : 1'bz;  // Controlled_Buffer controlled_buffer_4
endmodule

module Buffer_Invertido (
  input  [3:0] in_1,
  input  in_2,
  output [3:0] out_3
);

  assign out_3[3] = in_2 ? ~in_1[3] : 1'bz;  // Controlled_Inverter controlled_inverter_1
  assign out_3[2] = in_2 ? ~in_1[2] : 1'bz;  // Controlled_Inverter controlled_inverter_2
  assign out_3[1] = in_2 ? ~in_1[1] : 1'bz;  // Controlled_Inverter controlled_inverter_3
  assign out_3[0] = in_2 ? ~in_1[0] : 1'bz;  // Controlled_Inverter controlled_inverter_4
endmodule

module Decoder (
  input  [2:0] A,
  output S0,
  output S1,
  output S2,
  output S3,
  output S4,
  output S5,
  output S6,
  output S7
);

  wire and_1_out, and_2_out, and_3_out, and_4_out, and_5_out, and_6_out, and_7_out, and_8_out, not_1_out,
       not_2_out, not_3_out, not_4_out, not_5_out, not_6_out, not_7_out, not_8_out, not_9_out, not_10_out,
       not_11_out, not_12_out;

  not not_1 (not_1_out, A[2]);
  not not_2 (not_2_out, A[1]);
  not not_3 (not_3_out, A[2]);
  not not_4 (not_4_out, A[1]);
  not not_5 (not_5_out, A[2]);
  not not_6 (not_6_out, A[2]);
  not not_7 (not_7_out, A[1]);
  not not_8 (not_8_out, A[1]);
  and and_1 (and_1_out, A[2], A[1]);
  not not_9 (not_9_out, A[0]);
  and and_2 (and_2_out, A[2], A[1]);
  and and_3 (and_3_out, not_1_out, not_2_out);
  not not_10 (not_10_out, A[0]);
  and and_4 (and_4_out, not_3_out, not_4_out);
  and and_5 (and_5_out, not_5_out, A[1]);
  not not_11 (not_11_out, A[0]);
  and and_6 (and_6_out, not_6_out, A[1]);
  and and_7 (and_7_out, A[2], not_7_out);
  not not_12 (not_12_out, A[0]);
  and and_8 (and_8_out, A[2], not_8_out);
  and and_9 (S6, and_1_out, not_9_out);
  and and_10 (S7, and_2_out, A[0]);
  and and_11 (S0, and_3_out, not_10_out);
  and and_12 (S1, and_4_out, A[0]);
  and and_13 (S2, and_5_out, not_11_out);
  and and_14 (S3, and_6_out, A[0]);
  and and_15 (S4, and_7_out, not_12_out);
  and and_16 (S5, and_8_out, A[0]);
endmodule

module Rot_L (
  input  [3:0] ABCD,
  input  [1:0] XY,
  output [3:0] abcd_2
);

  wire and_1_out, and_2_out, and_3_out, and_4_out, and_5_out, and_6_out, and_7_out, and_8_out, and_9_out;

  and and_1 (and_1_out, ~XY[1], ~XY[0], ABCD[3]);  // AND_Gate
  and and_2 (and_2_out, ~XY[1], XY[0], ABCD[2]);  // AND_Gate
  and and_3 (and_3_out, XY[1], ~XY[0], ABCD[1]);  // AND_Gate
  and and_4 (and_4_out, XY[1], XY[0], ABCD[0]);
  and and_5 (and_5_out, ~XY[1], ~XY[0], ABCD[2]);  // AND_Gate
  and and_6 (and_6_out, ~XY[1], XY[0], ABCD[1]);  // AND_Gate
  and and_7 (and_7_out, XY[1], ~XY[0], ABCD[0]);  // AND_Gate
  and and_8 (and_8_out, ~XY[1], ~XY[0], ABCD[1]);  // AND_Gate
  and and_9 (and_9_out, ~XY[1], XY[0], ABCD[0]);  // AND_Gate
  and and_10 (abcd_2[0], ~XY[1], ~XY[0], ABCD[0]);  // AND_Gate
  or or_1 (abcd_2[3], and_1_out, and_2_out, and_3_out, and_4_out);
  or or_2 (abcd_2[2], and_5_out, and_6_out, and_7_out);
  or or_3 (abcd_2[1], and_8_out, and_9_out);
endmodule

module Rot_R (
  input  [3:0] ABCD,
  input  [1:0] XY,
  output [3:0] abcd_2
);

  wire and_1_out, and_2_out, and_3_out, and_4_out, and_5_out, and_6_out, and_7_out, and_8_out, and_9_out;

  and and_1 (and_1_out, ~XY[1], ~XY[0], ABCD[0]);  // AND_Gate
  and and_2 (and_2_out, ~XY[1], XY[0], ABCD[1]);  // AND_Gate
  and and_3 (and_3_out, XY[1], ~XY[0], ABCD[2]);  // AND_Gate
  and and_4 (and_4_out, XY[1], XY[0], ABCD[3]);
  and and_5 (and_5_out, ~XY[1], ~XY[0], ABCD[1]);  // AND_Gate
  and and_6 (and_6_out, ~XY[1], XY[0], ABCD[2]);  // AND_Gate
  and and_7 (and_7_out, XY[1], ~XY[0], ABCD[3]);  // AND_Gate
  and and_8 (and_8_out, ~XY[1], ~XY[0], ABCD[2]);  // AND_Gate
  and and_9 (and_9_out, ~XY[1], XY[0], ABCD[3]);  // AND_Gate
  and and_10 (abcd_2[3], ~XY[1], ~XY[0], ABCD[3]);  // AND_Gate
  or or_1 (abcd_2[0], and_1_out, and_2_out, and_3_out, and_4_out);
  or or_2 (abcd_2[1], and_5_out, and_6_out, and_7_out);
  or or_3 (abcd_2[2], and_8_out, and_9_out);
endmodule

module Or (
  input  [3:0] A,
  input  [3:0] B,
  output [3:0] S
);

  or or_1 (S[3], A[3], B[3]);
  or or_2 (S[1], A[1], B[1]);
  or or_3 (S[0], A[0], B[0]);
  or or_4 (S[2], A[2], B[2]);
endmodule

module ULA (
  input  D,
  input  [3:0] A,
  input  [3:0] B,
  input  [2:0] \Operações ,
  output Overflow,
  output [3:0] out_6,
  output Zero
);

  wire add4_1_overflow, and_1_out, and_2_out, decoder_1_s0, decoder_1_s1, decoder_1_s2, decoder_1_s3,
       decoder_1_s4, decoder_1_s5, decoder_1_s6, decoder_1_s7, not_1_out, sub4_1_overflow;
  wire [3:0] add4_1_soma, buffer_5_out_3, or_2_s, rot_l_1_abcd_2, rot_r_1_abcd_2, \sub4_1_subtração ;

  or or_1 (Overflow, and_1_out, and_2_out);
  and and_1 (and_1_out, sub4_1_overflow, decoder_1_s2);
  and and_2 (and_2_out, add4_1_overflow, decoder_1_s1);
  Decoder decoder_1 (
    .A(\Operações ), .S0(decoder_1_s0), .S1(decoder_1_s1), .S2(decoder_1_s2), .S3(decoder_1_s3),
    .S4(decoder_1_s4), .S5(decoder_1_s5), .S6(decoder_1_s6), .S7(decoder_1_s7));
  Buffer buffer_1 (.in_1(B), .out_3(out_6), .in_2(decoder_1_s0));
  nor nor_1 (Zero, decoder_1_s6, decoder_1_s7, out_6[0], out_6[1], out_6[2], out_6[3]);
  Add4 add4_1 (.A(B), .B(A), .OVERFLOW(add4_1_overflow), .CARRY_IN(1'b0), .SOMA(add4_1_soma));
  Buffer buffer_2 (.in_1(add4_1_soma), .out_3(out_6), .in_2(decoder_1_s1));
  Sub4 sub4_1 (.A(B), .B(A), .OVERFLOW(sub4_1_overflow), .CARRY_IN(1'b0), .\SUBTRAÇÃO (\sub4_1_subtração ));
  Buffer buffer_3 (.in_1(\sub4_1_subtração ), .out_3(out_6), .in_2(decoder_1_s2));
  Buffer_Invertido buffer_invertido_1 (.in_1(B), .in_2(decoder_1_s3), .out_3(out_6));
  Or or_2 (.A(B), .B(A), .S(or_2_s));
  Buffer buffer_4 (.in_1(or_2_s), .out_3(out_6), .in_2(decoder_1_s4));
  Rot_R rot_r_1 (.abcd_2(rot_r_1_abcd_2), .ABCD(A), .XY(B[1:0]));
  Rot_L rot_l_1 (.abcd_2(rot_l_1_abcd_2), .ABCD(A), .XY(B[1:0]));
  not not_1 (not_1_out, D);
  Buffer buffer_5 (.in_1(rot_r_1_abcd_2), .out_3(buffer_5_out_3), .in_2(D));
  Buffer buffer_6 (.in_1(rot_l_1_abcd_2), .out_3(buffer_5_out_3), .in_2(not_1_out));
  Buffer buffer_7 (.in_1(buffer_5_out_3), .out_3(out_6), .in_2(decoder_1_s5));
endmodule

module REG_AC (
  input  Clock,
  input  [3:0] D,
  output [3:0] D_2
);

  D_Flip_Flop D3 (.clk(Clock), .D(D[3]), .Q(D_2[3]));  // open: Qn, preset, en, reset
  D_Flip_Flop D2 (.clk(Clock), .D(D[2]), .Q(D_2[2]));  // open: Qn, preset, en, reset
  D_Flip_Flop D1 (.clk(Clock), .D(D[1]), .Q(D_2[1]));  // open: Qn, preset, en, reset
  D_Flip_Flop D0 (.clk(Clock), .D(D[0]), .Q(D_2[0]));  // open: Qn, preset, en, reset
endmodule

module MUX (
  input  [3:0] E,
  input  [3:0] D,
  input  in_3,
  output [3:0] out_4
);

  wire not_1_out;

  Buffer buffer_1 (.in_1(E), .out_3(out_4), .in_2(not_1_out));
  not not_1 (not_1_out, in_3);
  Buffer buffer_2 (.in_1(D), .out_3(out_4), .in_2(in_3));
endmodule

module IR (
  input  Clock,
  input  [7:0] D,
  output [7:0] D_2
);

  D_Flip_Flop #(.trigger("falling")) D3 (.clk(Clock), .D(D[7]), .Q(D_2[7]));  // open: Qn, preset, en, reset
  D_Flip_Flop #(.trigger("falling")) D2 (.clk(Clock), .D(D[6]), .Q(D_2[6]));  // open: Qn, preset, en, reset
  D_Flip_Flop #(.trigger("falling")) D1 (.clk(Clock), .D(D[5]), .Q(D_2[5]));  // open: Qn, preset, en, reset
  D_Flip_Flop #(.trigger("falling")) D0 (.clk(Clock), .D(D[4]), .Q(D_2[4]));  // open: Qn, preset, en, reset
  D_Flip_Flop #(.trigger("falling")) D3_2 (.clk(Clock), .D(D[3]), .Q(D_2[3]));  // open: Qn, preset, en, reset
  D_Flip_Flop #(.trigger("falling")) D2_2 (.clk(Clock), .D(D[2]), .Q(D_2[2]));  // open: Qn, preset, en, reset
  D_Flip_Flop #(.trigger("falling")) D1_2 (.clk(Clock), .D(D[1]), .Q(D_2[1]));  // open: Qn, preset, en, reset
  D_Flip_Flop #(.trigger("falling")) D0_2 (.clk(Clock), .D(D[0]), .Q(D_2[0]));  // open: Qn, preset, en, reset
endmodule

module Unidade_de_controle (
  input  [7:0] \Instrução ,
  input  Clock,
  input  Reset,
  input  Overflow,
  input  Zero,
  output [3:0] \B_Endereços ,
  output [3:0] Dado,
  output [3:0] Operando,
  output clk_RI,
  output clk_PC,
  output Rst_PC,
  output clk_AC,
  output \Direção ,
  output clk_RAM,
  output E,
  output [2:0] \Operação ,
  output out_17,
  output Load
);

  wire and_1_out, and_2_out, and_5_out, nand_2_out;
  wire [1:0] counter_1_q;

  nand nand_1 (out_17, \Instrução [7], \Instrução [6], \Instrução [5], \Instrução [4], clk_AC);
  and and_1 (and_1_out, \Instrução [7], \Instrução [6], \Instrução [5], ~\Instrução [4], clk_PC);  // AND_Gate
  Counter #(.width(2), .max('h3)) counter_1 (.Q(counter_1_q), .clk(Clock), .clr(Reset));  // open: load, D, count, carry
  and and_2 (and_2_out, \Instrução [7], \Instrução [6], ~\Instrução [5], \Instrução [4], clk_PC, Overflow);  // AND_Gate
  or or_1 (Load, and_1_out, and_2_out, and_5_out);
  and and_3 (clk_RI, ~counter_1_q[0], ~counter_1_q[1]);  // AND_Gate
  and and_4 (clk_PC, counter_1_q[0], ~counter_1_q[1]);  // AND_Gate
  and and_5 (and_5_out, \Instrução [7], \Instrução [6], ~\Instrução [5], ~\Instrução [4], clk_PC, Zero);  // AND_Gate
  and and_6 (clk_RAM, counter_1_q[0], counter_1_q[1]);
  and and_7 (clk_AC, ~counter_1_q[0], counter_1_q[1]);  // AND_Gate
  and and_8 (E, \Instrução [4], nand_2_out);
  nand nand_2 (nand_2_out, \Instrução [7], ~\Instrução [6], \Instrução [5]);  // NAND_Gate

  assign \B_Endereços  = \Instrução [3:0];
  assign Dado = \Instrução [3:0];
  assign \Direção  = \Instrução [4];
  assign Operando = \Instrução [3:0];
  assign \Operação  = \Instrução [7:5];
  assign Rst_PC = Reset;
endmodule
